# Fritzing sketch Display 7 Segmentos Con Raspberry (saved by Fritzing 0.9.3b)
breadboards: 1

parts:
  Raspberry_Pi_1 = Raspberry Pi 3 [part_number=RPI-3-V1.2]
  7_Segment1 = 7 Segment Display
  R3 = Resistor [tolerance=±5% resistance=220 package="1206 [SMD]"]
  R4 = Resistor [tolerance=±5% resistance=220 package="1206 [SMD]"]
  R5 = Resistor [tolerance=±5% resistance=220 package="1206 [SMD]"]
  R6 = Resistor [tolerance=±5% resistance=220 package="1206 [SMD]"]
  R7 = Resistor [tolerance=±5% resistance=220 package="1206 [SMD]"]
  R9 = Resistor [tolerance=±5% resistance=220 package="1206 [SMD]"]
  R10 = Resistor [tolerance=±5% resistance=220 package="1206 [SMD]"]

nets:
  N1: Raspberry_Pi_1.GIPO17, R9.Pin_0
  N2: Raspberry_Pi_1.GIPO27, R10.Pin_0
  N3: Raspberry_Pi_1.GIPO12, R4.Pin_0
  N4: Raspberry_Pi_1.GIPO23, R7.Pin_1
  N5: Raspberry_Pi_1.GIPO18, R6.Pin_1
  N6: Raspberry_Pi_1.GIPO15, R5.Pin_1
  N7: Raspberry_Pi_1.GIPO14, R3.Pin_0
  N8: Raspberry_Pi_1.GND, 7_Segment1.common_anode
  N9: 7_Segment1.Segment_E, R10.Pin_1
  N10: 7_Segment1.Segment_D, R9.Pin_1
  N11: 7_Segment1.Segment_C, R7.Pin_0
  N12: 7_Segment1.Segment_B, R6.Pin_0
  N13: 7_Segment1.Segment_A, R5.Pin_0
  N14: 7_Segment1.Segment_F, R3.Pin_1
  N15: 7_Segment1.Segment_G, R4.Pin_1
